# Fritzing sketch hc05 (saved by Fritzing 0.9.3b)
breadboards: 1

parts:
  Componente1 = Arduino Uno (Rev3)
  Componente2 = Bluetooth HC-05 Macho
  R1 = Resistor [tolerance=±5% resistance=1k package=THT]
  R2 = Resistor [tolerance=±5% resistance=330 package=THT]
  R3 = Resistor [tolerance=±5% resistance=330 package=THT]
  L298N1 = L298N DC motor driver
  M1 = DC Motor
  M2 = DC Motor
  VCC1 = Battery block 9V  # not connected

nets:
  GND: Componente1.GND, Componente2.GND, R3.Pin_1
  N1: Componente1.D0/RX, R1.Pin_1, R3.Pin_0
  N2: Componente1.D1/TX, Componente2.TXD
  N3: Componente1.D4, L298N1.IN1
  N4: Componente1.D5_PWM, L298N1.IN2
  N5: Componente1.D6_PWM, L298N1.IN3
  N6: Componente1.D7, L298N1.IN4
  5V: Componente1.5V, Componente2.VCC
  N7: Componente2.RXD, R1.Pin_0, R2.Pin_1
  N8: L298N1.OUT1, M1.pin_2
  N9: L298N1.OUT2, M1.pin_1
  N10: L298N1.OUT4, M2.pin_1

custom parts:
  L298N DC motor driver: 2x DC motor driver with 78M05 positive voltage regulator (7..35 V) L298N: max 46 V, 2 A Set 5 V Enable jumper to enable 5 V regultor (needed for the L298N) and +5 V output at screw terminal or supply external +5 V at screw terminal Set ENA and/or ENB to +5 V to enable motor permanently or supply ENA and/or ENB with PWM signal IN1 and IN2 set rotation directory for motor A (OUT1/OUT2) IN2 and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
